# Fritzing sketch Otopark (saved by Fritzing 0.9.3b)
breadboards: 1

parts:
  Parça1 = RFID USB Reader
  J1 = Basic Servo
  Parça2 = Arduino Uno (Rev3) - ICSP
  J2 = Piezo Speaker
  U1 = LCD-16X2 [package=lcd-16x2]
  Yeşil_Led = LED - 5mm [color="Red (633nm)" package="5 mm [THT]"]
  LED2 = smd LED [color="Red (633nm)" package="0805 [SMD]"]

nets:
  N1: Parça1.GNDT, Parça2.D10_PWM/SS
  N2: Parça1.CP, Parça2.D13/SCK
  N3: Parça1.ANT2, Parça2.D11_PWM/MOSI
  N4: Parça1.ANT1, Parça2.ICSP_MISO, Parça2.D12/MISO
  N5: Parça1.TX-O, Parça2.D9_PWM
  GND: Parça1.GND, J1.gnd, Parça2.GND, J2.pin1, U1.VSS, U1.VO, U1.R_W, U1.K, Yeşil_Led.cathode, LED2.cathode
  VCC: Parça1.VCC, Parça2.3V3
  VCC_2: J1.vcc, Parça2.5V, U1.VDD, U1.A
  N6: J1.pulse, Parça2.D6_PWM
  N7: Parça2.A0, U1.DB7
  N8: Parça2.A1, U1.DB6
  N9: Parça2.A2, U1.DB5
  N10: Parça2.A3, U1.DB4
  N11: Parça2.A4/SDA, U1.E
  N12: Parça2.A5/SCL, U1.RS
  N13: Parça2.D8, LED2.anode
  N14: Parça2.D5_PWM, J2.pin2
  N15: Parça2.D7, Yeşil_Led.anode
